# Fritzing sketch HC05_Arduino_Wiring (saved by Fritzing 0.9.2b)
breadboards: 1

parts:
  Part1 = Bluetooth HC-05 Macho
  Part2 = Arduino Uno (Rev3)

nets:
  N1: Part1.TXD, Part2.D10_PWM/SS
  N2: Part1.RXD, Part2.D11_PWM/MOSI
  VCC: Part1.VCC, Part2.5V
  GND: Part1.GND, Part2.GND
