# Fritzing sketch HC05_Arduino_Wiring_w_VoltageDivider (saved by Fritzing 0.9.2b)
breadboards: 1

parts:
  Part1 = Bluetooth HC-05 Macho
  Part2 = Arduino Uno (Rev3)
  R1 = Resistor [tolerance=±5% resistance=4.7k package="0402 [SMD]"]
  R2 = Resistor [tolerance=±5% resistance=10k package="0402 [SMD]"]

nets:
  N1: Part1.TXD, Part2.D10_PWM/SS
  N2: Part1.RXD, R1.Pin_1, R2.Pin_0
  VCC: Part1.VCC, Part2.5V
  GND: Part1.GND, Part2.GND, R2.Pin_1
  N3: Part2.D11_PWM/MOSI, R1.Pin_0
